// Digital circuit CPU.dig as structural Verilog
module CPU (
  input  Clock
);

  wire ALU_c_out, ALU_zero, ALUOp0, ALUOp1, ALUSrcA, and_1_out, Bit_30, ControlUnit_iord,
       ControlUnit_pcsource0, ControlUnit_pcwrite, ControlUnit_pcwritecond, I_Type, IRWrite, Mem_Read,
       Mem_Write, MemToReg, or_1_out, RegWrite;
  wire [1:0] ALUSrcB;
  wire [2:0] Funct3;
  wire [3:0] alu_control_unit_2_1_operation, ControlUnit_ns_3, STATE_REG_q;
  wire [4:0] Instr_Reg_q_2, Instr_Reg_q_3, Instr_Reg_q_4;
  wire [6:0] Instr_Reg_q;
  wire [23:0] multiplexer_1_out_2;
  wire [31:0] A_reg_q, ALU_alu_out, ALU_out_q, B_reg_q, immediategenerator_1_imm, Mem_Dummy_d, MemDataReg_q,
       multiplexer_1_out, multiplexer_2_out, multiplexer_3_out, multiplexer_4_out, multiplexer_5_out, PC_q,
       RegFile_value1, RegFile_value2;
  wire [31:25] Instr_Reg_q_5;

  Register #(.Bits(32)) PC (.D(multiplexer_5_out), .C(Clock), .en(or_1_out), .Q(PC_q));
  or or_1 (or_1_out, ControlUnit_pcwrite, and_1_out);
  Multiplexer #(.Bits(32)) multiplexer_1 (
    .sel(ControlUnit_iord), .in_0(PC_q), .in_1(ALU_out_q),
    .out({multiplexer_1_out[31:26], multiplexer_1_out_2, multiplexer_1_out[1:0]}));
  and and_1 (and_1_out, ControlUnit_pcwritecond, ALU_zero);
  RAMDualPort #(.AddrBits(24), .Bits(32)) Mem_Dummy (
    .A(multiplexer_1_out_2), .Din(B_reg_q), .str(Mem_Write), .C(Clock), .ld(Mem_Read), .D(Mem_Dummy_d));
  Register #(.Bits(32)) Instr_Reg (
    .D(Mem_Dummy_d), .C(Clock), .en(IRWrite),
    .Q({Instr_Reg_q_5[31], Bit_30, Instr_Reg_q_5[29:25], Instr_Reg_q_4, Instr_Reg_q_3, Funct3, Instr_Reg_q_2, Instr_Reg_q[6], I_Type, Instr_Reg_q[4:0]}));
  Register #(.Bits(32)) MemDataReg (.D(Mem_Dummy_d), .C(Clock), .en(1'b1), .Q(MemDataReg_q));
  Register #(.Bits(4)) STATE_REG (.D(ControlUnit_ns_3), .C(Clock), .en(1'b1), .Q(STATE_REG_q));
  OPCodeControlUnit ControlUnit (
    .I0(Instr_Reg_q[0]), .I1(Instr_Reg_q[1]), .I2(Instr_Reg_q[2]), .I3(Instr_Reg_q[3]), .I4(Instr_Reg_q[4]),
    .I5(I_Type), .I6(Instr_Reg_q[6]), .S_0(STATE_REG_q[0]), .S_1(STATE_REG_q[1]), .S_2(STATE_REG_q[2]),
    .S_3(STATE_REG_q[3]), .PCWrite(ControlUnit_pcwrite), .PCWriteCond(ControlUnit_pcwritecond),
    .IorD(ControlUnit_iord), .MemWrite(Mem_Write), .MemRead(Mem_Read), .IRWrite(IRWrite),
    .MemtoReg(MemToReg), .PCSource0(ControlUnit_pcsource0), .ALUOp0(ALUOp0), .ALUOp1(ALUOp1),
    .ALUSrcB1(ALUSrcB[1]), .ALUSrcB0(ALUSrcB[0]), .ALUSrcA(ALUSrcA), .RegWrite(RegWrite),
    .NS_0(ControlUnit_ns_3[0]), .NS_1(ControlUnit_ns_3[1]), .NS_2(ControlUnit_ns_3[2]),
    .NS_3(ControlUnit_ns_3[3]));  // open: PCSource1, LuiSrc, JalControl, JalrControl
  Multiplexer #(.Bits(32)) multiplexer_2 (
    .sel(MemToReg), .in_0(ALU_out_q), .in_1(MemDataReg_q), .out(multiplexer_2_out));
  ImmediateGenerator immediategenerator_1 (
    .Ins({Instr_Reg_q_5[31], Bit_30, Instr_Reg_q_5[29:25], Instr_Reg_q_4, Instr_Reg_q_3, Funct3, Instr_Reg_q_2, Instr_Reg_q[6], I_Type, Instr_Reg_q[4:0]}),
    .imm(immediategenerator_1_imm));
  RegFile32Bit RegFile (
    .DataToWrite(multiplexer_2_out), .writeEnable(RegWrite), .writeReg(Instr_Reg_q_2), .Read1(Instr_Reg_q_3),
    .Read2(Instr_Reg_q_4), .CPU_clock(Clock), .value1(RegFile_value1), .value2(RegFile_value2));
  Register #(.Bits(32)) A_reg (.D(RegFile_value1), .C(Clock), .en(1'b1), .Q(A_reg_q));
  Register #(.Bits(32)) B_reg (.D(RegFile_value2), .C(Clock), .en(1'b1), .Q(B_reg_q));
  Multiplexer #(.Bits(32)) multiplexer_3 (.sel(ALUSrcA), .in_0(PC_q), .in_1(A_reg_q), .out(multiplexer_3_out));
  Multiplexer #(.Selector_Bits(2), .Bits(32)) multiplexer_4 (
    .sel(ALUSrcB), .in_0(B_reg_q), .in_1(32'h4), .in_2(immediategenerator_1_imm), .in_3({32{1'b0}}),
    .out(multiplexer_4_out));
  alu_control_unit_2 alu_control_unit_2_1 (
    .ALUop({ALUOp1, ALUOp0}), .F({Bit_30, Funct3}), .Itype(I_Type), .Operation(alu_control_unit_2_1_operation));
  ALU32Bit ALU (
    .Operation(alu_control_unit_2_1_operation), .a(multiplexer_3_out), .b(multiplexer_4_out),
    .c_out(ALU_c_out), .ALU_out(ALU_alu_out), .zero(ALU_zero));
  Multiplexer #(.Bits(32)) multiplexer_5 (
    .sel(ControlUnit_pcsource0), .in_0(ALU_alu_out), .in_1(ALU_out_q), .out(multiplexer_5_out));
  Register #(.Bits(32)) ALU_out (.D(ALU_alu_out), .C(Clock), .en(1'b1), .Q(ALU_out_q));
endmodule
